# Fritzing sketch nano_huits_leds (saved by Fritzing 0.9.4)

parts:
  LED2 = smd LED [color="Green (570nm)" package="1206 [SMD]"]
  LED3 = smd LED [color="Green (570nm)" package="1206 [SMD]"]
  LED4 = smd LED [color="Green (570nm)" package="1206 [SMD]"]
  LED5 = smd LED [color="Green (570nm)" package="1206 [SMD]"]
  LED6 = smd LED [color="Green (570nm)" package="1206 [SMD]"]
  LED7 = smd LED [color="Green (570nm)" package="1206 [SMD]"]
  LED8 = smd LED [color="Green (570nm)" package="1206 [SMD]"]
  LED1 = smd LED [color="Green (570nm)" package="1206 [SMD]"]
  R1 = Resistor [tolerance=±5% resistance=220 package="0805 [SMD]"]
  R2 = Resistor [tolerance=±5% resistance=220 package="0805 [SMD]"]
  R3 = Resistor [tolerance=±5% resistance=220 package="0805 [SMD]"]
  R4 = Resistor [tolerance=±5% resistance=220 package="0805 [SMD]"]
  R5 = Resistor [tolerance=±5% resistance=220 package="0805 [SMD]"]
  R6 = Resistor [tolerance=±5% resistance=220 package="0805 [SMD]"]
  R7 = Resistor [tolerance=±5% resistance=220 package="0805 [SMD]"]
  R8 = Resistor [tolerance=±5% resistance=220 package="0805 [SMD]"]
  GND = female pin header, 9 pins [form="♀ (female)"]
  Composant2 = Arduino Nano (Rev3.0)

nets:
  N1: LED2.cathode, GND.pin2
  N2: LED3.cathode, GND.pin3
  N3: LED4.cathode, GND.pin4
  N4: LED5.cathode, GND.pin5
  N5: LED6.cathode, GND.pin6
  N6: LED7.cathode, GND.pin7
  N7: LED8.cathode, GND.pin8
  N8: LED1.cathode, GND.pin1
  N9: R1.Pin_1, Composant2.D4
  N10: R2.Pin_1, Composant2.D5
  N11: R3.Pin_1, Composant2.D6
  N12: R4.Pin_1, Composant2.D7
  N13: R5.Pin_1, Composant2.D8
  N14: R6.Pin_1, Composant2.D9
  N15: R7.Pin_1, Composant2.D10
  N16: R8.Pin_1, Composant2.D11/MOSI
  N17: GND.pin9, Composant2.GND

notes:
  L6
  L1
  L2
  L3
  L4
  L5
  L8
  L7
