# Fritzing sketch 2boutons_4leds_2servos_arduino_uno (saved by Fritzing 0.9.4)

parts:
  R8 = Resistor [tolerance=±5% resistance=10k package=THT]
  J2 = female pin header, 2 pins [form="♀ (female)"]
  S2 = Momentary Switch [package=ksa_sealed_tac_switch]
  Composant1 = Arduino Uno (Rev3) - ICSP
  LED1 = smd LED [color="Blue (525nm)" package="1206 [SMD]"]
  R17 = Resistor [tolerance=±5% resistance=220 package=THT]
  S3 = Momentary Switch [package=ksa_sealed_tac_switch]
  LED2 = smd LED [color="Blue (525nm)" package="1206 [SMD]"]
  R18 = Resistor [tolerance=±5% resistance=220 package=THT]
  BAT1 = BC9VPC [package=bc9vpc]
  JACK1 = 2.1mm Barrel Jack with Terminal Block
  PCB2 = PCB 4 boutons poussoirs GND commun [package=THT]
  R19 = Resistor [tolerance=±5% resistance=10k package=THT]
  J4 = male pin header, 8 pins [form="♂ (male)"]
  J5 = longpad pin header, 8 pins [form="long pad"]
  C2 = Ceramic Capacitor [capacitance=100nF voltage=35V package="100 mil [THT, multilayer]"]
  LED3 = smd LED [color="Blue (525nm)" package="1206 [SMD]"]
  LED4 = smd LED [color="Blue (525nm)" package="1206 [SMD]"]
  C3 = Ceramic Capacitor [capacitance=100nF voltage=35V package="100 mil [THT, multilayer]"]
  R20 = Resistor [tolerance=±5% resistance=220 package=THT]
  R21 = Resistor [tolerance=±5% resistance=220 package=THT]
  J9 = Basic Servo
  J10 = Basic Servo
  J8 = female pin header, 4 pins [form="♀ (female)"]
  J7 = female pin header, 10 pins [form="♀ (female)"]

nets:
  N1: R8.Pin_0, PCB2.pin10
  N2: R8.Pin_1, PCB2.pin15
  N3: J2.pin1, PCB2.pin9, J7.pin1
  N4: J2.pin2, PCB2.pin14, J8.pin1
  N5: S2.2, PCB2.pin30, J5.pin4
  N6: S2.4, J7.pin4
  N7: Composant1.D8, R20.Pin_1
  N8: Composant1.D9_PWM, J10.pulse
  N9: Composant1.D10_PWM/SS, J9.pulse
  N10: Composant1.D11_PWM/MOSI, R21.Pin_1
  N11: Composant1.D4, PCB2.pin20, J4.pin2
  N12: Composant1.D5_PWM, PCB2.pin22, J4.pin4
  N13: Composant1.D6_PWM, R18.Pin_1
  N14: Composant1.D7, R17.Pin_1
  N15: Composant1.5V, J8.pin2
  N16: Composant1.GND, J7.pin2
  N17: LED1.cathode, J7.pin5
  N18: S3.1, PCB2.pin28, J5.pin2
  N19: S3.3, J7.pin3
  N20: LED2.cathode, J7.pin6
  N21: BAT1.V+, JACK1.POS
  N22: PCB2.pin11, R19.Pin_0
  N23: PCB2.pin16, R19.Pin_1
  N24: PCB2.pin19, J4.pin1
  N25: PCB2.pin21, J4.pin3
  N26: PCB2.pin23, J4.pin5
  N27: PCB2.pin24, J4.pin6
  N28: PCB2.pin25, J4.pin7
  N29: PCB2.pin26, J4.pin8
  N30: PCB2.pin27, J5.pin1
  N31: PCB2.pin29, J5.pin3
  N32: PCB2.pin31, J5.pin5
  N33: PCB2.pin32, J5.pin6
  N34: PCB2.pin33, J5.pin7
  N35: PCB2.pin34, J5.pin8
  N36: PCB2.pin35, C3.1
  N37: PCB2.pin36, C3.0
  N38: PCB2.pin37, C2.1
  N39: PCB2.pin38, C2.0
  N40: LED3.cathode, J7.pin7
  N41: LED4.cathode, J7.pin8
  N42: J9.gnd, J7.pin9
  N43: J9.vcc, J8.pin3
  N44: J10.gnd, J7.pin10
  N45: J10.vcc, J8.pin4

custom parts:
  PCB 4 boutons poussoirs GND commun: Circuit imprimé 4 boutons poussoirs GND commun
