# Fritzing sketch uno_huit_leds (saved by Fritzing 0.9.4)

parts:
  Composant1 = Arduino Uno (Rev3) - ICSP
  LED2 = smd LED [color="Green (570nm)" package="1206 [SMD]"]
  LED3 = smd LED [color="Green (570nm)" package="1206 [SMD]"]
  LED4 = smd LED [color="Green (570nm)" package="1206 [SMD]"]
  LED5 = smd LED [color="Green (570nm)" package="1206 [SMD]"]
  LED6 = smd LED [color="Green (570nm)" package="1206 [SMD]"]
  LED7 = smd LED [color="Green (570nm)" package="1206 [SMD]"]
  LED8 = smd LED [color="Green (570nm)" package="1206 [SMD]"]
  LED1 = smd LED [color="Green (570nm)" package="1206 [SMD]"]
  R1 = Resistor [tolerance=±5% resistance=220 package="0805 [SMD]"]
  R2 = Resistor [tolerance=±5% resistance=220 package="0805 [SMD]"]
  R3 = Resistor [tolerance=±5% resistance=220 package="0805 [SMD]"]
  R4 = Resistor [tolerance=±5% resistance=220 package="0805 [SMD]"]
  R5 = Resistor [tolerance=±5% resistance=220 package="0805 [SMD]"]
  R6 = Resistor [tolerance=±5% resistance=220 package="0805 [SMD]"]
  R7 = Resistor [tolerance=±5% resistance=220 package="0805 [SMD]"]
  R8 = Resistor [tolerance=±5% resistance=220 package="0805 [SMD]"]
  GND = female pin header, 9 pins [form="♀ (female)"]

nets:
  N1: Composant1.D8, R5.Pin_1
  N2: Composant1.D9_PWM, R6.Pin_1
  N3: Composant1.D10_PWM/SS, R7.Pin_1
  N4: Composant1.D11_PWM/MOSI, R8.Pin_1
  N5: Composant1.GND, GND.pin9
  N6: Composant1.D4, R1.Pin_1
  N7: Composant1.D5_PWM, R2.Pin_1
  N8: Composant1.D6_PWM, R3.Pin_1
  N9: Composant1.D7, R4.Pin_1
  N10: LED2.cathode, GND.pin2
  N11: LED3.cathode, GND.pin3
  N12: LED4.cathode, GND.pin4
  N13: LED5.cathode, GND.pin5
  N14: LED6.cathode, GND.pin6
  N15: LED7.cathode, GND.pin7
  N16: LED8.cathode, GND.pin8
  N17: LED1.cathode, GND.pin1

notes:
  L6
  L1
  L2
  L3
  L4
  L5
  L8
  L7
