# Fritzing sketch mega2560_mini_huit_leds (saved by Fritzing 0.9.4)

parts:
  LED2 = smd LED [color="Green (570nm)" package="1206 [SMD]"]
  LED3 = smd LED [color="Green (570nm)" package="1206 [SMD]"]
  LED4 = smd LED [color="Green (570nm)" package="1206 [SMD]"]
  LED5 = smd LED [color="Green (570nm)" package="1206 [SMD]"]
  LED6 = smd LED [color="Green (570nm)" package="1206 [SMD]"]
  LED7 = smd LED [color="Green (570nm)" package="1206 [SMD]"]
  LED8 = smd LED [color="Green (570nm)" package="1206 [SMD]"]
  LED1 = smd LED [color="Green (570nm)" package="1206 [SMD]"]
  R1 = Resistor [tolerance=±5% resistance=220 package="0805 [SMD]"]
  R2 = Resistor [tolerance=±5% resistance=220 package="0805 [SMD]"]
  R3 = Resistor [tolerance=±5% resistance=220 package="0805 [SMD]"]
  R4 = Resistor [tolerance=±5% resistance=220 package="0805 [SMD]"]
  R5 = Resistor [tolerance=±5% resistance=220 package="0805 [SMD]"]
  R6 = Resistor [tolerance=±5% resistance=220 package="0805 [SMD]"]
  R7 = Resistor [tolerance=±5% resistance=220 package="0805 [SMD]"]
  R8 = Resistor [tolerance=±5% resistance=220 package="0805 [SMD]"]
  GND = female pin header, 9 pins [form="♀ (female)"]
  M3 = Mega2560 R3 Pro Mini

nets:
  N1: LED2.cathode, GND.pin2
  N2: LED3.cathode, GND.pin3
  N3: LED4.cathode, GND.pin4
  N4: LED5.cathode, GND.pin5
  N5: LED6.cathode, GND.pin6
  N6: LED7.cathode, GND.pin7
  N7: LED8.cathode, GND.pin8
  N8: LED1.cathode, GND.pin1
  N9: R1.Pin_1, M3.4▀
  N10: R2.Pin_1, M3.5▀
  N11: R3.Pin_1, M3.6▀
  N12: R4.Pin_1, M3.7▀
  N13: R5.Pin_1, M3.8▀
  N14: R6.Pin_1, M3.9▀
  N15: R7.Pin_1, M3.10▀
  N16: R8.Pin_1, M3.11▀
  N17: GND.pin9, M3.GND

notes:
  L6
  L1
  L2
  L3
  L4
  L5
  L8
  L7

custom parts:
  Mega2560 R3 Pro Mini: The Mega 2560 R3 Pro Mini :- Completely compatible with original Arduino Mega2560 Pin pitch: 0.1 inch Size: 5.42cm*3.68cm With Atmega16U2 chip as the USB to Serial converter 5V working voltage. Input Voltage:7-12V Analog Input Pins: 16 Digital I/O pins: 54 The Mega 2560 R3 Pro Mini has no datasheet and no info and I don't have one to compare, so I made this based on photos. Dec 2019 modified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
