# Fritzing sketch ESP01_UNO_adaptateur_WIFI (saved by Fritzing 0.9.4)

parts:
  Composant1 = Arduino Uno (Rev3) - ICSP
  LED2 = smd LED [color="Green (570nm)" package="1206 [SMD]"]
  LED3 = smd LED [color="Green (570nm)" package="1206 [SMD]"]
  LED4 = smd LED [color="Green (570nm)" package="1206 [SMD]"]
  LED5 = smd LED [color="Green (570nm)" package="1206 [SMD]"]
  LED6 = smd LED [color="Green (570nm)" package="1206 [SMD]"]
  LED7 = smd LED [color="Green (570nm)" package="1206 [SMD]"]
  LED8 = smd LED [color="Green (570nm)" package="1206 [SMD]"]
  LED1 = smd LED [color="Green (570nm)" package="1206 [SMD]"]
  R1 = Resistor [tolerance=±5% resistance=220 package="0805 [SMD]"]
  R2 = Resistor [tolerance=±5% resistance=220 package="0805 [SMD]"]
  R3 = Resistor [tolerance=±5% resistance=220 package="0805 [SMD]"]
  R4 = Resistor [tolerance=±5% resistance=220 package="0805 [SMD]"]
  R5 = Resistor [tolerance=±5% resistance=220 package="0805 [SMD]"]
  R6 = Resistor [tolerance=±5% resistance=220 package="0805 [SMD]"]
  R7 = Resistor [tolerance=±5% resistance=220 package="0805 [SMD]"]
  R8 = Resistor [tolerance=±5% resistance=220 package="0805 [SMD]"]
  GND = female pin header, 9 pins [form="♀ (female)"]
  Adapter_ESP2 = Adapter ESP_01 [chip_label="Adapter ESP-01" package=THT]
  U2 = ESP8266 WiFi Module [part_number=ESP8266]

nets:
  N1: Composant1.D8, R5.Pin_1
  N2: Composant1.D9_PWM, R6.Pin_1
  N3: Composant1.D10_PWM/SS, R7.Pin_1
  N4: Composant1.D11_PWM/MOSI, R8.Pin_1
  GND: Composant1.GND, GND.pin9, Adapter_ESP2.GND
  N5: Composant1.D2, Adapter_ESP2.RX
  N6: Composant1.D3_PWM, Adapter_ESP2.TX
  N7: Composant1.D4, R1.Pin_1
  N8: Composant1.D5_PWM, R2.Pin_1
  N9: Composant1.D6_PWM, R3.Pin_1
  N10: Composant1.D7, R4.Pin_1
  N11: Composant1.5V, Adapter_ESP2.VCC_5V
  N12: LED2.cathode, GND.pin2
  N13: LED3.cathode, GND.pin3
  N14: LED4.cathode, GND.pin4
  N15: LED5.cathode, GND.pin5
  N16: LED6.cathode, GND.pin6
  N17: LED7.cathode, GND.pin7
  N18: LED8.cathode, GND.pin8
  N19: LED1.cathode, GND.pin1
  GND_2: Adapter_ESP2.gnd, U2.GND
  N20: Adapter_ESP2.gpio2, U2.GPIO_2
  N21: Adapter_ESP2.gpio, U2.GPIO_0
  N22: Adapter_ESP2.rxd, U2.RXD
  N23: Adapter_ESP2.txd, U2.TXD
  N24: Adapter_ESP2.ch_pd, U2.CH_PD
  N25: Adapter_ESP2.rst, U2.RST
  N26: Adapter_ESP2.vcc_3v, U2.VCC

notes:
  L6
  L1
  L2
  L3
  L4
  L5
  L8
  L7

custom parts:
  Adapter ESP_01: A dummy, proxy, ersatz, stand-in part for whatever you want. With 12 pins on a 100 mil inline pin header footprint.
  ESP8266 WiFi Module: Generic WiFi Module based on the ESP8266 with onboard PCB antenna and UART communications
