# Fritzing sketch flash_DT06_FTD1232 (saved by Fritzing 0.9.4)

parts:
  Adaptateur = PCB pour HC-06 [package=THT]
  R11 = Resistor [tolerance=±5% resistance=2.2k package=THT]
  R12 = Resistor [tolerance=±5% resistance=1k package=THT]
  DT06 = Wifi DT06
  FTD1232 = FTD1232
  J1 = female pin header, 2 pins [form="♀ (female)"]

nets:
  N1: Adaptateur.pin1, DT06.RXD
  N2: Adaptateur.pin2, DT06.TXD
  N3: Adaptateur.pin3, DT06.GND
  N4: Adaptateur.pin4, DT06.VCC
  N5: Adaptateur.pin5, R12.Pin_0
  N6: Adaptateur.pin6, R11.Pin_0
  N7: Adaptateur.pin7, R12.Pin_1
  N8: Adaptateur.pin8, R11.Pin_1
  N9: Adaptateur.pin9, FTD1232.TXO
  N10: Adaptateur.pin10, FTD1232.RXI
  N11: Adaptateur.pin11, FTD1232.GND
  N12: Adaptateur.pin12, FTD1232.POWER
  N13: J1.pin1, J1.pin2

custom parts:
  PCB pour HC-06: PcB pour contrôler bluetooth HC06
  FTD1232: Description: This is the newest revision of our FTD 1232
