# Fritzing sketch hc_&_dt-06 (saved by Fritzing 0.9.4)
circuit board: 1.10166cm x 1.92758cm

parts:
  2kohm = Resistor [tolerance=±5% resistance=220 package=THT]
  J2 = female pin header, 4 pins [form="♀ (female)"]
  1Kohm = Resistor [tolerance=±5% resistance=220 package=THT]
  HC-06 = female pin header, 4 pins [form="♀ (female)"]

nets:
  N1: 2kohm.Pin_0, 1Kohm.Pin_0, HC-06.pin4
  N2: 2kohm.Pin_1, J2.pin2, HC-06.pin2
  N3: J2.pin1, HC-06.pin1
  N4: J2.pin3, HC-06.pin3
  N5: J2.pin4, 1Kohm.Pin_1

notes:
  +5v
  GND
  TXD
  RXD
